# Fritzing sketch artikle (saved by Fritzing 0.9.3b)
breadboards: 1

parts:
  LCM1602_IIC2 = LCM1602 IIC [part_number="LCM1602 IIC" chip_label="LCM1602 IIC" package="DIP (Dual Inline) [THT]"]
  LCD1 = LCD screen
  Часть1 = Arduino Leonardo (Rev3b)
  Matrix_keypad1 = KEYPAD 4x4
  LED1 = smd LED [color="Green (565nm)" package="0603 [SMD]"]
  LED2 = smd LED [color="Red (633nm)" package="0603 [SMD]"]
  J1 = Piezo Speaker
  J2 = Basic Servo

nets:
  VSS: LCM1602_IIC2.VSS, LCD1.VSS
  VDD: LCM1602_IIC2.VDD, LCD1.VDD
  N1: LCM1602_IIC2.V0, LCD1.V0
  N2: LCM1602_IIC2.RS, LCD1.RS
  N3: LCM1602_IIC2.RW, LCD1.R/W
  N4: LCM1602_IIC2.E, LCD1.E
  N5: LCM1602_IIC2.D0, LCD1.DB0
  N6: LCM1602_IIC2.D1, LCD1.DB1
  N7: LCM1602_IIC2.D2, LCD1.DB2
  N8: LCM1602_IIC2.D3, LCD1.DB3
  N9: LCM1602_IIC2.D4, LCD1.DB4
  N10: LCM1602_IIC2.D5, LCD1.DB5
  N11: LCM1602_IIC2.D6, LCD1.DB6
  N12: LCM1602_IIC2.D7, LCD1.DB7
  N13: LCM1602_IIC2.A, LCD1.LED+
  N14: LCM1602_IIC2.K, LCD1.LED-
  GND: LCM1602_IIC2.GND, Часть1.GND, LED1.cathode, LED2.cathode, J1.pin1, J2.gnd
  VCC: LCM1602_IIC2.VCC, Часть1.5V, J2.vcc
  N15: LCM1602_IIC2.SDA, Часть1.A4
  N16: LCM1602_IIC2.SCL, Часть1.A5
  N17: LCM1602_IIC2.LED_A, LCM1602_IIC2.LED_B
  N18: Часть1.D2/SDA, Matrix_keypad1.row3
  N19: Часть1.D3_PWM/SCL, Matrix_keypad1.row2
  N20: Часть1.D4/A6, Matrix_keypad1.row1
  N21: Часть1.D5_PWM, Matrix_keypad1.col4
  N22: Часть1.D6_PWM/A7, Matrix_keypad1.col3
  N23: Часть1.D7, Matrix_keypad1.col2
  N24: Часть1.D8/A8, Matrix_keypad1.col1
  N25: Часть1.D10_PWM/A10, J2.pulse
  N26: Часть1.D11_PWM, LED2.anode
  N27: Часть1.D12/A11, LED1.anode
  N28: Часть1.D13_PWM, J1.pin2

custom parts:
  LCM1602 IIC: I2C-Module to use a 1602 or 2004 LCD on with the wire.h libory Serial LCD Modul
  KEYPAD 4x4: Matrix keypad 16 buttons, 4 rows x 4 columns
